// Logisim project circuits.circ as structural Verilog: 3 circuits, main circuit MyXOR
module MyXOR (
  input  X,
  input  Y,
  output Output
);

  wire and_1_out, and_2_out, not_1_out, not_2_out;

  FullAdder fulladder_1 ();  // open: X, Y, CarryIn, sum, CarryOut
  not not_1 (not_1_out, X);
  not not_2 (not_2_out, Y);
  _4_bit_Ripple_Carry_Adder u_4_bit_ripple_carry_adder_1 ();  // open: Y3, X3, Y2, X2, Y1, X1, Y0, X0, Sum4, Sum3, Sum2, Sum1, Sum0
  and and_1 (and_1_out, not_1_out, Y);
  and and_2 (and_2_out, X, not_2_out, not_2_out);
  or or_1 (Output, and_1_out, and_1_out, and_2_out);

  // Notes on the sheet:
  //   Here is a location to build an XOR circuit
  //   We already implemented this circuit in class.  Copy it here.
endmodule

module FullAdder (
  input  X,
  input  Y,
  input  CarryIn,
  output sum,
  output CarryOut
);

  wire and_1_out, and_2_out;

  // AND_Gate and_1 has open pins: out=and_1_out
  // AND_Gate and_2 has open pins: out=and_2_out
  or or_1 (CarryOut, and_1_out, and_2_out);
endmodule

module _4_bit_Ripple_Carry_Adder (
  input  Y3,
  input  Y2,
  input  Y1,
  input  Y0,
  input  X3,
  input  X2,
  input  X1,
  input  X0,
  output Sum4,
  output Sum3,
  output Sum2,
  output Sum1,
  output Sum0
);
endmodule
